// Logisim project logisim_circ.circ as structural Verilog
module twos_comp (
  input  [7:0] num_in,
  output [7:0] out_2
);

  wire or_2_out, or_3_out, or_4_out, or_5_out, or_6_out, or_7_out;

  // OR_Gate or_1 has open pins: in0=num_in[7], in1=or_2_out, out=open
  xor xor_1 (out_2[7], num_in[7], or_2_out);
  or or_2 (or_2_out, num_in[6], or_3_out);
  xor xor_2 (out_2[6], num_in[6], or_3_out);
  or or_3 (or_3_out, num_in[5], or_4_out);
  xor xor_3 (out_2[5], num_in[5], or_4_out);
  or or_4 (or_4_out, num_in[4], or_5_out);
  xor xor_4 (out_2[4], num_in[4], or_5_out);
  or or_5 (or_5_out, num_in[3], or_6_out);
  xor xor_5 (out_2[3], num_in[3], or_6_out);
  or or_6 (or_6_out, num_in[2], or_7_out);
  or or_7 (or_7_out, num_in[1], num_in[0]);
  xor xor_6 (out_2[2], num_in[2], or_7_out);
  xor xor_7 (out_2[1], num_in[1], num_in[0]);

  assign out_2[0] = num_in[0];
endmodule

module FullAdder (
  input  X,
  input  Y,
  input  Cin,
  output S,
  output Cout
);

  wire and_1_out, and_2_out, and_3_out;

  xor xor_1 (S, X, Y, Cin);
  and and_1 (and_1_out, X, Y);
  and and_2 (and_2_out, Y, Cin);
  and and_3 (and_3_out, X, Cin);
  or or_1 (Cout, and_1_out, and_2_out, and_3_out);
endmodule

module FourBitRCA (
  input  [3:0] Y,
  input  [3:0] X,
  input  Cin
);

  wire fulladder_1_cout, fulladder_1_s, fulladder_2_cout, fulladder_2_s, fulladder_3_cout, fulladder_3_s,
       fulladder_4_cout, fulladder_4_s;

  FullAdder fulladder_1 (.X(X[0]), .Y(Y[0]), .Cin(Cin), .S(fulladder_1_s), .Cout(fulladder_1_cout));
  FullAdder fulladder_2 (.X(X[3]), .Y(Y[3]), .Cin(fulladder_4_cout), .S(fulladder_2_s), .Cout(fulladder_2_cout));
  FullAdder fulladder_3 (.X(X[1]), .Y(Y[1]), .Cin(fulladder_1_cout), .S(fulladder_3_s), .Cout(fulladder_3_cout));
  FullAdder fulladder_4 (.X(X[2]), .Y(Y[2]), .Cin(fulladder_3_cout), .S(fulladder_4_s), .Cout(fulladder_4_cout));
endmodule
